# Fritzing sketch watering (saved by Fritzing 0.9.2b)
circuit board: 8.46667cm x 5.64444cm
breadboards: 1

parts:
  Part1 = Arduino Pro Mini v13
  R1 = Resistor [tolerance=±2% resistance=10k package=THT]
  R2 = Resistor [tolerance=±2% resistance=10k package=THT]
  S1 = Pushbutton [package="[THT]"]
  S2 = Pushbutton [package="[THT]"]
  LCM1602_IIC1 = LCM1602 IIC [part_number="LCM1602 IIC" chip_label="LCM1602 IIC" package="DIP (Dual Inline) [THT]"]
  IC1 = DS1302 [package="DIP8 [THT]"]
  LCD1 = LCD screen
  Y1 = CRYSTAL [package=crystal-32khz-smd]
  BAT1 = Battery Holders [package=battcon_12mm]
  U1 = Header 8 [package=1x08_smd]

nets:
  N1: Part1.A4, LCM1602_IIC1.SDA
  N2: Part1.A5, LCM1602_IIC1.SCL
  GND: Part1.GND, R1.Pin_1, R2.Pin_1, LCM1602_IIC1.GND, IC1.0V, BAT1.-, U1.1
  VCC: Part1.VCC, S1.Pin_1, S1.Pin_2, S2.Pin_1, S2.Pin_2, LCM1602_IIC1.VCC, IC1.+V
  N3: Part1.D13/SCK, U1.8
  N4: Part1.D12/MISO, U1.7
  N5: Part1.D11_PWM/MOSI, U1.6
  N6: Part1.D10_PWM/SS, U1.5
  N7: Part1.D9_PWM, U1.4
  N8: Part1.D8, IC1.CE_-_Chip_Enable
  N9: Part1.D7, IC1.I/O_-_SPI_Data_In/Out
  N10: Part1.D6_PWM, IC1.SCLK_-_SPI_Clock
  N11: Part1.D5_PWM, U1.3
  N12: Part1.D4, U1.2
  N13: Part1.D3_PWM, R1.Pin_0, S1.Pin_3, S1.Pin_4
  N14: Part1.D2, R2.Pin_0, S2.Pin_3, S2.Pin_4
  VSS: LCM1602_IIC1.VSS, LCD1.VSS
  VDD: LCM1602_IIC1.VDD, LCD1.VDD
  N15: LCM1602_IIC1.V0, LCD1.V0
  N16: LCM1602_IIC1.RS, LCD1.RS
  N17: LCM1602_IIC1.RW, LCD1.R/W
  N18: LCM1602_IIC1.E, LCD1.E
  N19: LCM1602_IIC1.D0, LCD1.DB0
  N20: LCM1602_IIC1.D1, LCD1.DB1
  N21: LCM1602_IIC1.D2, LCD1.DB2
  N22: LCM1602_IIC1.D3, LCD1.DB3
  N23: LCM1602_IIC1.D4, LCD1.DB4
  N24: LCM1602_IIC1.D5, LCD1.DB5
  N25: LCM1602_IIC1.D6, LCD1.DB6
  N26: LCM1602_IIC1.D7, LCD1.DB7
  N27: LCM1602_IIC1.A, LCD1.LED+
  N28: LCM1602_IIC1.K, LCD1.LED-
  N29: IC1.X1_-_Crystal, Y1.2
  N30: IC1.X2_-_Crystal, Y1.1
  N31: IC1.Vbat_-_Backup_Supply, BAT1.+

custom parts:
  LCM1602 IIC: I2C-Module to use a 1602 or 2004 LCD on with the wire.h libory Serial LCD Modul

// code stored in the sketch: watering.ino
#include <stdio.h>
#include <DS1302.h>
#include <Wire.h>
#include <LiquidCrystal_I2C.h>
#include <EEPROM.h>

// Set the LCD address to 0x27 for a 16 chars and 2 line display
LiquidCrystal_I2C lcd(0x27, 16, 2);

DS1302 rtc(8, 7, 6);

const int BUTTON_1 = 2;
const int BUTTON_2 = 3;

const int OUTPUT_PORT_1 = 4;
const int OUTPUT_PORT_2 = 9;
const int OUTPUT_PORT_3 = 10;
const int OUTPUT_PORT_4 = 11;
const int OUTPUT_PORT_5 = 12;

const int TOTAL_PORT = 5;

int OUTPUT_PINS[TOTAL_PORT] = {OUTPUT_PORT_1, OUTPUT_PORT_2, OUTPUT_PORT_3, OUTPUT_PORT_4, OUTPUT_PORT_5};

boolean lastButton1 = LOW;
boolean currentButton1 = LOW;
boolean lastButton2 = LOW;
boolean currentButton2 = LOW;

const float timeout = 60.0;
const int TOTAL_JOBS = 20;

int menuType = 0;

struct Job {
    uint8_t duration; // running time second
    uint8_t schedAt; // schedule at second

    byte port; // the output port

    boolean repeat; // every day, once
    boolean running;
    boolean enable; // enable or disable
};

String dayAsString(const Time::Day day) {
    switch (day) {
        case Time::kSunday: return "Sun";
        case Time::kMonday: return "Mon";
        case Time::kTuesday: return "Tue";
        case Time::kWednesday: return "Wed";
        case Time::kThursday: return "Thu";
        case Time::kFriday: return "Fri";
        case Time::kSaturday: return "Sat";
    }
    return "err";
}

boolean backToMenu() {
    int count = 0;
    while (count < 10) {
        delay(100);
        currentButton1 = debounce(BUTTON_1, lastButton1);
        if (currentButton1 == LOW) {
            break;
        }
        count += 1;
    }
    lastButton1 = currentButton1;
    if (currentButton1 == HIGH) {
        return true;
    }

    return false;
}

void printTime(Time t) {
    // Name the day of the week.
    const String day = dayAsString(t.day);

    // Format the time and date and insert into the temporary buffer.
    char line1[16];
    snprintf(line1, sizeof(line1), "%04d-%02d-%02d %s", t.yr, t.mon, t.date, day.c_str());

    char line2[16];
    snprintf(line2, sizeof(line2), "%02d:%02d:%02d", t.hr, t.min, t.sec);

    // Print the formatted string to serial so we can see the time.
    lcd.setCursor(0, 0);
    lcd.print(line1);
    lcd.setCursor(0, 1);
    lcd.print(line2);
}

void setup() {
    // initialize the LCD
    lcd.begin();

    // Turn on the blacklight and print a message.
    lcd.backlight();

    // Initialize a new chip by turning off write protection and clearing the
    // clock halt flag. These methods needn't always be called. See the DS1302
    // datasheet for details.
    rtc.writeProtect(false);
    rtc.halt(false);

    pinMode(BUTTON_1, INPUT);
    pinMode(BUTTON_2, INPUT);
    for (int i=0;i<TOTAL_PORT;i++) {
        pinMode(OUTPUT_PINS[i], OUTPUT);
    }
    // pinMode(OUTPUT_PIN, OUTPUT);
}

boolean debounce(int BUTTON, boolean last) {
    boolean current = digitalRead(BUTTON);
    if (last != current) {
        delay(5);
        current = digitalRead(BUTTON);
    }

    return current;
}

void settingTime(Time t) {
    // lcd.cursor();
    lcd.blink();
    int type = 0;
    boolean isChanged = false;
    boolean isChangedMinute = false;
    boolean isChangedSecond = false;
    boolean rerender = true;
    float waiting = 0;
    while (1) {
        waiting += 0.1;
        if (waiting > timeout) {
           break;
        }
        if (rerender) {
            rerender = false;
            printTime(t);
            switch(type) {
            case 0: // year
                lcd.setCursor(0, 0);
                break;
            case 1: // month
                lcd.setCursor(5, 0);
                break;
            case 2: // date
                lcd.setCursor(8, 0);
                break;
            case 3: // day
                lcd.setCursor(11, 0);
                break;
            case 4: // hour
                lcd.setCursor(0, 1);
                break;
            case 5: // minute
                lcd.setCursor(3, 1);
                break;
            case 6: // second
                lcd.setCursor(6, 1);
                break;
            }
        }
        currentButton2 = debounce(BUTTON_2, lastButton2);
        if (lastButton2 == LOW && currentButton2 == HIGH) {
            rerender = true;
            waiting = 0;
            isChanged = true;
            switch(type) {
            case 0: // year
                t.yr += 1;
                if (t.yr > 2030) {
                    t.yr = 2015;
                }
                break;
            case 1: // month
                t.mon += 1;
                if (t.mon > 12) {
                    t.mon = 1;
                }
                break;
            case 2: // date
                t.date += 1;
                switch (t.mon) {
                case 1:
                case 3:
                case 5:
                case 7:
                case 8:
                case 10:
                case 12:
                    if (t.date > 31) {
                        t.date = 1;
                    }
                    break;
                case 4:
                case 6:
                case 9:
                case 11:
                    if (t.date > 30) {
                        t.date = 1;
                    }
                    break;
                case 2:
                    if (t.yr % 400 == 0 || (t.yr % 4 == 0 && t.yr % 100 != 0)) {
                        if (t.date > 29) {
                            t.date = 1;
                        }
                    } else {
                        if (t.date > 28) {
                            t.date = 1;
                        }
                    }
                    break;
                }
                break;
            case 3: // day
                switch (t.day) {
                    case Time::kSunday:
                        t.day = Time::kMonday;
                        break;
                    case Time::kMonday:
                        t.day = Time::kThursday;
                        break;
                    case Time::kTuesday:
                        t.day = Time::kWednesday;
                        break;
                    case Time::kWednesday:
                        t.day = Time::kTuesday;
                        break;
                    case Time::kThursday:
                        t.day = Time::kFriday;
                        break;
                    case Time::kFriday:
                        t.day = Time::kSaturday;
                        break;
                    case Time::kSaturday:
                        t.day = Time::kSunday;
                        break;
                }
                break;
            case 4: // hour
                t.hr += 1;
                if (t.hr > 23) {
                    t.hr = 0;
                }
                break;
            case 5: // minute
                isChangedMinute = true;
                t.min += 1;
                if (t.min > 59) {
                    t.min = 0;
                }
                break;
            case 6: // second
                isChangedSecond = true;
                t.sec += 1;
                if (t.sec > 59) {
                    t.sec = 0;
                }
                break;
            }
        }
        lastButton2 = currentButton2;

        currentButton1 = debounce(BUTTON_1, lastButton1);
        if (lastButton1 == LOW && currentButton1 == HIGH) {
            waiting = 0;
            rerender = true;
            type += 1;
            if (type > 5 || backToMenu()) {
                lastButton1 = currentButton1;
                break;
            }
        }
        lastButton1 = currentButton1;

        Time currentTime = rtc.time();
        if (!isChangedMinute) {
            t.min = currentTime.min;
        }
        if (!isChangedSecond) {
            if (t.sec != currentTime.sec) {
                rerender = true;
            }
            t.sec = currentTime.sec;
        }

        delay(100);
    }
    lcd.noBlink();
    if (isChanged) {
        Time currentTime = rtc.time();
        if (!isChangedMinute) {
            t.min = currentTime.min;
        }
        if (!isChangedSecond) {
            t.sec = currentTime.sec;
        }
        rtc.time(t);
    }
    menuType = 0;
}

void printJobs() {
    lcd.clear();
    lcd.setCursor(0, 0);
    Job job;
    int jobID = 0;
    int eeAddress = 0;
    char line[16];
    boolean rerender = true;

    float waiting = 0;
    int hour, minute, second, remain;
    while (1) {
        waiting += 0.1;
        if (waiting > timeout) {
           break;
        }

        if (rerender) {
            waiting = 0;
            rerender = false;
            EEPROM.get(eeAddress, job);

            hour = job.schedAt / 3600;
            remain = job.schedAt % 3600;
            minute = remain / 60;
            second = remain % 60;
            snprintf(line, sizeof(line), "#%02d %02d:%02d:%02d", jobID, hour, minute, second);
            lcd.setCursor(0, 0);
            lcd.print(line);
            lcd.setCursor(13, 0);
            if (job.enable) {
                lcd.print(" on");
            } else {
                lcd.print("off");
            }

            hour = job.duration / 3600;
            remain = job.duration % 3600;
            minute = remain / 60;
            second = remain % 60;
            snprintf(line, sizeof(line), "durat: %02d:%02d:%02d", hour, minute, second);
            lcd.setCursor(0, 1);
            lcd.print(line);
        }

        currentButton2 = debounce(BUTTON_2, lastButton2);
        if (lastButton2 == LOW && currentButton2 == HIGH) {
            rerender = true;
            eeAddress += sizeof(job);
            jobID += 1;
            if (jobID > TOTAL_JOBS) {
                jobID = 0;
                eeAddress = 0;
            }
        }
        lastButton2 = currentButton2;

        currentButton1 = debounce(BUTTON_1, lastButton1);
        if (lastButton1 == LOW && currentButton1 == HIGH) {

            if (backToMenu()) {
                break;
            }

            editJob(jobID, eeAddress);
            rerender = true;
        }
        lastButton1 = currentButton1;
        delay(100);
    }
    menuType = 0;
    lcd.clear();
}

void editJob(int jobID, int eeAddress) {
    Job job;
    EEPROM.get(eeAddress, job);
    boolean rerender = true;
    int step = 0;
    char line[16];
    lcd.blink();
    float waiting = 0;
    int remain;
    int hour = job.schedAt / 3600;
    remain = job.schedAt % 3600;
    int minute = remain / 60;
    int second = remain % 60;

    int duration_hour = job.duration / 3600;
    remain = job.duration % 3600;
    int duration_minute = remain / 60;
    int duration_second = remain % 60;
    while (1) {
        waiting += 0.1;
        if (waiting > timeout) {
           break;
        }
        if (rerender) {
            waiting = 0;
            rerender = false;
            lcd.clear();
            switch (step) {
                case 0:
                case 1:
                case 2:
                case 3:
                case 4:
                case 5:
                case 6:
                    snprintf(line, sizeof(line), "#%02d %02d:%02d:%02d", jobID, hour, minute, second);
                    lcd.setCursor(0, 0);
                    lcd.print(line);
                    lcd.setCursor(13, 0);
                    if (job.enable) {
                        lcd.print(" on");
                    } else {
                        lcd.print("off");
                    }

                    snprintf(line, sizeof(line), "durat: %02d:%02d:%02d", duration_hour, duration_minute, duration_second);
                    lcd.setCursor(0, 1);
                    lcd.print(line);
                    break;
                case 7:
                case 8:
                    lcd.setCursor(0, 0);
                    lcd.print("repeat:");
                    lcd.setCursor(13, 0);
                    if (job.repeat) {
                        lcd.print(" on");
                    } else {
                        lcd.print("off");
                    }
                    lcd.setCursor(0, 1);
                    lcd.print("port: ");
                    lcd.print(job.port + 1);
                    break;
            }
            switch (step) {
            case 0: // hour
                lcd.setCursor(4, 0);
                break;
            case 1: // minute
                lcd.setCursor(7, 0);
                break;
            case 2: // second
                lcd.setCursor(10, 0);
                break;
            case 3: // enable
                lcd.setCursor(13, 0);
                break;
            case 4: // duration hour
                lcd.setCursor(7, 1);
                break;
            case 5: // duration minute
                lcd.setCursor(10, 1);
                break;
            case 6: // duration second
                lcd.setCursor(13, 1);
                break;
            case 7: // repeat
                lcd.setCursor(13, 0);
                break;
            case 8: // port
                lcd.setCursor(6, 1);
                break;
            }
        }

        currentButton2 = debounce(BUTTON_2, lastButton2);
        if (lastButton2 == LOW && currentButton2 == HIGH) {
            rerender = true;
            switch (step) {
            case 0: // hour
                hour += 1;
                if (hour > 23) {
                    hour = 0;
                }
                break;
            case 1: // minute
                minute += 1;
                if (minute > 59) {
                    minute = 0;
                }
                break;
            case 2: // second
                second += 1;
                if (second > 59) {
                    second = 0;
                }
                break;
            case 3: // enable
                job.enable = !job.enable;
                break;
            case 4: // duration hour
                duration_hour += 1;
                if (duration_hour > 12) {
                    duration_hour = 0;
                }
                break;
            case 5: // duration minute
                duration_minute += 1;
                if (duration_minute > 59) {
                    duration_minute = 0;
                }
                break;
            case 6: // duration second
                duration_second += 1;
                if (duration_second > 59) {
                    duration_second = 0;
                }
                break;
            case 7: // repeat
                job.repeat = !job.repeat;
                break;
            case 8: // port
                job.port += 1;
                if (job.port >= TOTAL_PORT) {
                    job.port = 0;
                }
                break;
            }
        }
        lastButton2 = currentButton2;

        currentButton1 = debounce(BUTTON_1, lastButton1);
        if (lastButton1 == LOW && currentButton1 == HIGH) {
            rerender = true;
            step += 1;
            if (step > 8 || backToMenu()) {
                break;
            }
        }
        lastButton1 = currentButton1;
        delay(100);
    }
    lcd.noBlink();

    job.schedAt = hour * 3600 + minute * 60 + second;
    job.duration = duration_hour * 3600 + duration_minute * 60 + duration_second;
    EEPROM.put(eeAddress, job);
}

void resetJobs() {
    Job job = {
        0, // duration
        0, // schedAt
        0, // port
        false, // repeat
        false, // running
        false // enable
    };
    int eeAddress = 0;
    for (int i=0; i<=TOTAL_JOBS; i++) {
        EEPROM.put(eeAddress, job);
        eeAddress += sizeof(job);
    }
    menuType = 0;
}

void checkAndRunJobs(Time t) {
    int eeAddress = 0;
    Job job;
    boolean ports[TOTAL_PORT];

    for (int i=0;i<TOTAL_PORT;i++) {
        ports[i] = false;
    }

    int current = t.hr * 3600 + t.min * 60 + t.sec;
    for (int i=0; i<=TOTAL_JOBS; i++) {
        EEPROM.get(eeAddress, job);
        eeAddress += sizeof(job);
        if (!job.enable) {
            continue;
        }
        if (job.schedAt <= current && current <= job.schedAt + job.duration) {
            ports[job.port] = true;
        }
    }


    for (int i=0;i<TOTAL_PORT;i++) {
        digitalWrite(OUTPUT_PINS[i], ports[i]);
    }

}


int showMenu() {
    int select = 0;
    boolean rerender = true;
    lcd.blink();
    float waiting = 0;
    while (1) {
        waiting += 0.1;
        if (waiting > timeout) {
           break;
        }
        if (rerender) {
            waiting = 0;
            rerender = false;
            switch (select) {
            case 0:
                lcd.clear();
                lcd.setCursor(0, 0);
                lcd.print("1. show time");
                lcd.setCursor(0, 1);
                lcd.print("2. config time");
                lcd.setCursor(0, 0);
                break;
            case 1:
                lcd.clear();
                lcd.setCursor(0, 0);
                lcd.print("2. config time");
                lcd.setCursor(0, 1);
                lcd.print("3. show jobs");
                lcd.setCursor(0, 0);
                break;
            case 2:
            case 3:
                lcd.clear();
                lcd.setCursor(0, 0);
                lcd.print("3. show jobs");
                lcd.setCursor(0, 1);
                lcd.print("4. reset");
                lcd.setCursor(0, select % 2);
                break;
            }
        }
        currentButton2 = debounce(BUTTON_2, lastButton2);
        if (lastButton2 == LOW && currentButton2 == HIGH) {
            rerender = true;
            select += 1;
            if (select > 3) {
                select = 0;
            }
        }
        lastButton2 = currentButton2;

        currentButton1 = debounce(BUTTON_1, lastButton1);
        if (lastButton1 == LOW && currentButton1 == HIGH) {
            lastButton1 = currentButton1;
            break;
        }
        lastButton1 = currentButton1;
        delay(100);
    }
    lcd.noBlink();
    lcd.clear();
    return select;
}

// Loop and print the time every second.
void loop() {
    // Get the current time and date from the chip.
    Time t = rtc.time();

    switch (menuType) {
    case 0:
        printTime(t);
        break;
    case 1:
        settingTime(t);
        break;
    case 2:
        printJobs();
        break;
    case 3:
        resetJobs();
        break;
    }

    checkAndRunJobs(t);

    currentButton1 = debounce(BUTTON_1, lastButton1);
    if (lastButton1 == LOW && currentButton1 == HIGH) {
        lastButton1 = currentButton1;
        menuType = showMenu();
    }
    lastButton1 = currentButton1;
    delay(100);
}
